# Fritzing sketch apagarLEdInterruptor (saved by Fritzing 0.9.2b)
breadboards: 1

parts:
  Parte1 = Arduino Uno (Rev3)
  LED1 = LED - 5mm [color="Red (633nm)" package="5 mm [THT]"]  # not connected
  S1 = Pushbutton [package=THT]
  R1 = Resistor [tolerance=±5% resistance=220 package=THT]
  R2 = Resistor [tolerance=±5% resistance=3.3k package=THT]

nets:
  N1: Parte1.D8, S1.leg0, R1.Pin_1
  N2: Parte1.5V, S1.leg1
  N3: Parte1.GND, R1.Pin_0, R2.Pin_1
